# Fritzing sketch StreamMarker Relay 5V PCB mains powered (saved by Fritzing 0.9.2b)
circuit board: 8.54428cm x 5.64269cm
breadboards: 1

parts:
  XBee = XBEE-1 [package=xbee-silk]
  Raspberry_Pi = Raspberry Pi B rev2
  DS1621 = IC, DIP package, 8 pins [chip_label=DS1621 part_number=DS1621+-ND]
  4_7k = Resistor [tolerance=±5% resistance=4.7k package=THT]
  4_7k_2 = Resistor [tolerance=±5% resistance=4.7k package=THT]

nets:
  VDD: XBee.VDD, Raspberry_Pi.3V3, DS1621.pin8, 4_7k.Pin_0, 4_7k_2.Pin_0
  N1: XBee.DOUT, Raspberry_Pi.GPIO_15
  N2: XBee.DIN, Raspberry_Pi.GPIO_14
  GND: XBee.GND, Raspberry_Pi.GND, DS1621.pin4, DS1621.pin5, DS1621.pin6, DS1621.pin7
  N3: Raspberry_Pi.GPIO_2, DS1621.pin1, 4_7k.Pin_1
  N4: Raspberry_Pi.GPIO_3, DS1621.pin2, 4_7k_2.Pin_1

notes:
  StreamMarker Relay
  v1.0
