# Fritzing sketch StreamMarker Sensor 3.3V PCB mains powered (saved by Fritzing 0.9.2b)
circuit board: 10.7cm x 4.96cm
breadboards: 1

parts:
  Arduino_3v = Arduino Pro Mini v13
  XBee = XBEE-1 [package=xbee-silk]
  POWER = screw terminal, 2 pins
  S3 = screw terminal, 3 pins
  S2 = screw terminal, 3 pins
  S1 = screw terminal, 3 pins
  S4 = screw terminal, 3 pins
  DS1337 = IC, DIP package, 8 pins [chip_label=DS1337]
  32kHz_Crystal = Crystal [frequency="32 kHz" part_number=CFS-20632768DZFB package=THT]
  4_7k = Resistor [tolerance=±5% resistance=4.7k package=THT]
  DS1621 = IC, DIP package, 8 pins [chip_label=DS1621 part_number=DS1621+-ND]
  Ext_Temp = screw terminal, 3 pins
  4_7k_2 = Resistor [tolerance=±5% resistance=4.7k package=THT]
  4_7k_3 = Resistor [tolerance=±5% resistance=4.7k package=THT]

nets:
  N1: Arduino_3v.D1/RX, XBee.DOUT
  VCC: Arduino_3v.VCC, XBee.VDD, DS1337.pin8, 4_7k.Pin_0, DS1621.pin8, Ext_Temp.pin1, 4_7k_2.Pin_0, 4_7k_3.Pin_0
  N2: Arduino_3v.A4, DS1337.pin5, 4_7k.Pin_1, DS1621.pin1
  N3: Arduino_3v.A5, DS1337.pin6, DS1621.pin2, 4_7k_3.Pin_1
  N4: Arduino_3v.RAW, POWER.pin1, S3.pin1, S2.pin1, S1.pin1, S4.pin1
  GND: Arduino_3v.GND, XBee.GND, POWER.pin2, S3.pin3, S2.pin3, S1.pin3, S4.pin3, DS1337.pin4, DS1621.pin4, DS1621.pin5, DS1621.pin6, DS1621.pin7, Ext_Temp.pin3
  N5: Arduino_3v.A3, S4.pin2
  N6: Arduino_3v.A2, S3.pin2
  N7: Arduino_3v.A1, S2.pin2
  N8: Arduino_3v.A0, S1.pin2
  N9: Arduino_3v.D4, DS1337.pin7
  N10: Arduino_3v.D3_PWM, DS1337.pin3
  N11: Arduino_3v.D2, Ext_Temp.pin2, 4_7k_2.Pin_1
  N12: Arduino_3v.D0/TX, XBee.DIN
  N13: DS1337.pin1, 32kHz_Crystal.pin_0
  N14: DS1337.pin2, 32kHz_Crystal.pin_1

notes:
  StreamMarker Sensor
  v1.2
  +
  -
